# Fritzing sketch wiring diagram (saved by Fritzing 0.9.3b)

parts:
  Arduino_Uno = Arduino Uno (Rev3)
  photodiod_1 = KY-018 Photoresistor Module [package="Breakout board"]
  VCC1 = Battery block 9V
  photodiod_2 = KY-018 Photoresistor Module [package="Breakout board"]
  VCC2 = Battery block 9V
  photodiod_3 = KY-018 Photoresistor Module [package="Breakout board"]
  VCC3 = Battery block 9V
  SP1 = SPEAKER [package=pcb_mount_speaker]
  start_button = Round Pushbutton
  stop_button = Round Pushbutton
  LED1 = LED - 5mm [color="Red (633nm)" package="5 mm [THT]"]
  LED2 = LED - 5mm [color="Red (633nm)" package="5 mm [THT]"]
  LED3 = LED - 5mm [color="Red (633nm)" package="5 mm [THT]"]
  D1 = Rectifier Diode [part_number=1N4001 package="300 mil [THT]"]
  D2 = Rectifier Diode [part_number=1N4001 package="300 mil [THT]"]
  D3 = Rectifier Diode [part_number=1N4001 package="300 mil [THT]"]
  Laser3 = Red Laser diode [package="5 mm [THT]"]
  Laser2 = Red Laser diode [package="5 mm [THT]"]
  Laser1 = Red Laser diode [package="5 mm [THT]"]
  R7 = Resistor [tolerance=±5% resistance=10k package=THT]

nets:
  N1: Arduino_Uno.A0, D1.cathode, D2.cathode, D3.cathode, R7.Pin_1
  N2: Arduino_Uno.D9_PWM, SP1.-
  N3: Arduino_Uno.D11_PWM/MOSI, stop_button.leg0
  N4: Arduino_Uno.D12/MISO, start_button.leg0
  N5: Arduino_Uno.GND, photodiod_1.-, photodiod_2.-, photodiod_3.-, SP1.+, start_button.leg1, stop_button.leg1, LED1.cathode, LED2.cathode, LED3.cathode, R7.Pin_0
  VIN: Arduino_Uno.5V, photodiod_1.Vin, photodiod_2.Vin, photodiod_3.Vin
  N6: photodiod_1.S, LED1.anode, D1.anode
  N7: VCC1.-, Laser1.-
  N8: VCC1.+, Laser1.+
  N9: photodiod_2.S, LED2.anode, D2.anode
  N10: VCC2.-, Laser2.-
  N11: VCC2.+, Laser2.+
  N12: photodiod_3.S, LED3.anode, D3.anode
  N13: VCC3.-, Laser3.-
  N14: VCC3.+, Laser3.+

custom parts:
  KY-018 Photoresistor Module: KY-018 Photoresistor module, used to measure light intensity. It can determine the presence or absence of light.
  Red Laser diode: A generic red Laser
